# Fritzing sketch Umanoide Sketch (saved by Fritzing 0.9.3b)

parts:
  Arduino_Nano_v3 = Arduino Micro (Rev3)
  J1 = Basic Servo  # not connected
  GY1 = MPU-6050 Board GY-521 [form="♀ (female)" package=THT]
  Componente2 = Bi-Directional Logic Level Converter
  U3 = 74HC4017 [package="DIP16 [THT]"]
  U4 = 74HC4017 [package="DIP16 [THT]"]
  J2 = Basic Servo  # not connected
  J3 = Basic Servo  # not connected
  J4 = Basic Servo  # not connected
  J5 = Basic Servo  # not connected
  J6 = Basic Servo  # not connected
  J8 = Basic Servo  # not connected
  J9 = Basic Servo  # not connected
  J10 = Basic Servo  # not connected
  J11 = Basic Servo  # not connected
  J12 = Basic Servo  # not connected
  J13 = Basic Servo  # not connected
  J14 = Basic Servo  # not connected
  J15 = Basic Servo  # not connected
  J16 = Basic Servo  # not connected
  J17 = Basic Servo  # not connected
  J18 = Basic Servo  # not connected
  J19 = Basic Servo  # not connected
  J20 = Basic Servo  # not connected
  J21 = Basic Servo  # not connected
  J22 = Basic Servo  # not connected
  VCC1 = Battery  # not connected
  VCC2 = Battery  # not connected
  Componente3 = Bluetooth HC-05 Macho

nets:
  N1: Arduino_Nano_v3.D1/TX, Componente2.HV2
  N2: Arduino_Nano_v3.D0/RX, Componente2.HV1
  N3: Arduino_Nano_v3.D4_PWM/A6, U4.MR
  N4: Arduino_Nano_v3.D5_PWM, U4.CP0
  N5: Arduino_Nano_v3.D6_PWM/A7, U3.CP0
  N6: Arduino_Nano_v3.D7, U3.MR
  N7: Arduino_Nano_v3.SCK, Componente2.HV3
  N8: Arduino_Nano_v3.MISO, Componente2.HV4
  N9: Arduino_Nano_v3.GND, Componente2.GND#8
  5V: Arduino_Nano_v3.5V, Arduino_Nano_v3.3V3, GY1.pin1, Componente2.LV, Componente2.HV, Componente3.VCC
  N10: Arduino_Nano_v3.A5, GY1.pin3
  N11: Arduino_Nano_v3.A4, GY1.pin4
  N12: GY1.pin2, Componente2.GND#3, Componente3.GND
  N13: Componente2.LV1, Componente3.TXD
  N14: Componente2.LV2, Componente3.RXD

custom parts:
  MPU-6050 Board GY-521: Acelerometro y Giroscopio MPU-6050 Board GY-521
  Bi-Directional Logic Level Converter: Description: If you've ever tried to connect a 3.3V device to a 5V system, you know what a challenge it can be. The SparkFun bi-directional logic level converter is a small device that safely steps down 5V signals to 3.3V AND steps up 3.3V to 5V at the same time. This level converter also works with 2.8V and 1.8V devices. What really separates this Logic level converter from our previous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
  74HC4017: 5-stage Johnson decade counter
